// Logisim project fa.circ as structural Verilog: 3 circuits, main circuit main
module main (
  input  in_1,
  input  in_2,
  input  in_3
);

  wire fulladder_1_c, fulladder_1_s;

  FullAdder fulladder_1 (.z(in_1), .x(in_2), .y(in_3), .s(fulladder_1_s), .c(fulladder_1_c));
endmodule

module HalfAdder (
  input  x,
  input  y,
  output s,
  output c
);

  xor xor_1 (s, x, y);
  and and_1 (c, x, y);
endmodule

module FullAdder (
  input  z,
  input  x,
  input  y,
  output s,
  output c
);

  wire halfadder_1_c, halfadder_1_s, halfadder_2_c;

  HalfAdder halfadder_1 (.x(x), .y(y), .s(halfadder_1_s), .c(halfadder_1_c));
  HalfAdder halfadder_2 (.x(z), .y(halfadder_1_s), .s(s), .c(halfadder_2_c));
  or or_1 (c, halfadder_2_c, halfadder_1_c);

  // Notes on the sheet:
  //   x and y are the 2 input bits and z is the carry in
endmodule
